// Digital circuit fetch.dig as structural Verilog
module fetch (
  input  C,
  output error,
  output halt
);

  wire C_t, decoder_1_out_0, decoder_2_p2, err;
  wire [1:0] priorityencoder_1_num;
  wire [5:0] PC_out;
  wire [15:0] halt_t, IR_q, ramdualport_1_d;

  PriorityEncoder #(.Selector_Bits(2)) priorityencoder_1 (
    .in0(1'b1), .in1(halt_t[0]), .in2(err), .in3(1'b0), .num(priorityencoder_1_num));  // open: any
  Decoder #(.Selector_Bits(2)) decoder_1 (
    .sel(priorityencoder_1_num), .out_0(decoder_1_out_0), .out_1(halt), .out_2(error));  // open: out_3
  Counter #(.Bits(6)) PC (.en(1'b1), .C(C_t), .clr(1'b0), .out(PC_out), .ovf(err));
  and and_1 (C_t, C, decoder_1_out_0);
  RAMDualPort #(.AddrBits(6), .isProgramMemory("true"), .Bits(16)) ramdualport_1 (
    .A(PC_out), .Din({16{1'b0}}), .str(1'b0), .C(C_t), .ld(1'b1), .D(ramdualport_1_d));
  Register #(.Bits(16)) IR (.D(ramdualport_1_d), .C(C_t), .en(1'b1), .Q(IR_q));
  // decoder decoder_2: pin names not known; wires that end beside it: IR_q, decoder_2_p2, halt_t
  // Probe on decoder_2_p2
endmodule
